# Fritzing sketch tp1 (saved by Fritzing 0.9.4)
breadboards: 1

parts:
  Composant1 = Arduino Uno (Rev3)
  LED1 = LED - 5mm [color="Red (633nm)" package="5 mm [THT]"]
  S1 = Pushbutton [package="[THT]"]
  R1 = Resistor [tolerance=±5% resistance=1k package=THT]

nets:
  N1: Composant1.D12/MISO, LED1.anode
  N2: Composant1.GND, LED1.cathode, R1.Pin_1
  N3: Composant1.D2, S1.Pin_1, S1.Pin_2, R1.Pin_0
  N4: Composant1.5V, S1.Pin_3, S1.Pin_4
