# Fritzing sketch tp4 (saved by Fritzing 0.9.4)
breadboards: 1

parts:
  Composant1 = Arduino Uno (Rev3)
  R2 = Resistor [tolerance=±5% resistance=4.7k package=THT]
  R3 = Resistor [tolerance=±5% resistance=1k package=THT]
  R4 = Resistor [tolerance=±5% resistance=1k package=THT]
  R5 = Resistor [tolerance=±5% resistance=1k package=THT]
  R6 = Rotary Potentiometer (Small) [maximum_resistance=100kΩ package=THT]
  S1 = Pushbutton [package="[THT]"]
  R7 = Resistor [tolerance=±5% resistance=1k package=THT]

nets:
  N1: Composant1.A0, R2.Pin_1, R3.Pin_0
  N2: Composant1.A1, R5.Pin_0, R6.leg2
  N3: Composant1.GND, R3.Pin_1, R5.Pin_1, R7.Pin_1
  N4: Composant1.D2, Composant1.5V, R6.wiper, S1.Pin_3, S1.Pin_4, R7.Pin_0
  N5: R2.Pin_0, R4.Pin_1
  N6: S1.Pin_1, S1.Pin_2
